# Fritzing sketch Rally_Droid2 (saved by Fritzing 0.8.5b)
breadboards: 1

parts:
  Espessif_Serial_Wifi_Modul_1 = ESP8266 ESP01 [part_number=ESP8266 package=THT]
  S1 = H-Bridge with L298N
  U1 = V_REG_LD1117VXX [package=78xxl]
  VCC1 = Battery block 9V
  M1 = DC Motor
  M2 = DC Motor  # not connected
  Part1 = Arduino Mega 2560 (Rev3)
  Part2 = SRF05 Ultrasonic Rangefinder
  LED1 = LED - 5mm [color="Blue (470nm)" package="5 mm [THT]"]
  LED2 = LED - 5mm [color="Red (633nm)" package="5 mm [THT]"]
  LED3 = LED - 5mm [color="Red (633nm)" package="5 mm [THT]"]
  DHT1 = DHT11 Humitidy and Temperature Sensor
  Part3 = RFID-RC522-v2
  RTC1 = DS1307 RTC Breakout

nets:
  GND: Espessif_Serial_Wifi_Modul_1.GND, S1.GND, U1.GND, VCC1.-, Part1.GND, Part2.GND, LED1.anode, LED2.anode, LED3.anode, DHT1.GND, Part3.GND, RTC1.GND
  N1: Espessif_Serial_Wifi_Modul_1.RXD, Part1.D18/TX1
  N2: Espessif_Serial_Wifi_Modul_1.TXD, Part1.D19/RX1
  N3: Espessif_Serial_Wifi_Modul_1.VCC, U1.OUT, Part3.3_3V
  N4: S1.12V, U1.IN, VCC1.+
  5V: S1.5V, Part1.5V, Part2.VCC, DHT1.VDD, RTC1.5V
  N5: S1.IN1, Part1.D4_PWM
  N6: S1.IN2, Part1.D5_PWM
  N7: S1.IN3, Part1.D6_PWM
  N8: S1.IN4, Part1.D7_PWM
  N9: S1.OUT4-Motor2, M1.pin_1
  N10: Part1.D21/SCL, RTC1.SCL
  N11: Part1.D20/SDA, RTC1.SDA
  N12: Part1.D13_PWM, LED1.cathode
  N13: Part1.D12_PWM, LED3.cathode
  N14: Part1.D11_PWM, LED2.cathode
  N15: Part1.D10_PWM, Part2.Echo
  N16: Part1.D9_PWM, Part2.Trig
  N17: Part1.D2_PWM, DHT1.DATA
  N18: Part1.D49, Part3.RST
  N19: Part1.D50, Part3.MISO
  N20: Part1.D51, Part3.MOSI
  N21: Part1.D52, Part3.SCK
  N22: Part1.D53, Part3.SDA

notes:
  HC-SR04
  L298N
  arduino pin 8 for enA and pin 3 enB
  esp8266-01
  RFID-RC522
  DHT11
  Mega2560
  3,3v regulator
  TCRT5000+LM939 IR line tracking sensor module x 2 (left and right)
  RTC DS1307

custom parts:
  ESP8266 ESP01: Generic WiFi Module based on the ESP8266 with onboard PCB antenna and UART communications
  H-Bridge with L298N: h-bridge
  DHT11 Humitidy and Temperature Sensor: DHT11 Humidity and Temperature Sensor
  RFID-RC522-v2: A simple China made RFID-RC522 Reader; do check the pin labels, as this is a MFRC522 based clone.
  DS1307 RTC Breakout: DS1307 Real-time Clock Breakout Board with Battery
